# Fritzing sketch Schéma (saved by Fritzing 0.9.3b)
circuit board: 8.46667cm x 5.64444cm

parts:
  Raspberry_Pi_1 = Raspberry Pi 3 [part_number=RPI-3-V1.2]
  Play_Pause = Pushbutton [package="[SMD]"]
  Back = Pushbutton [package="[SMD]"]
  R1 = Resistor [tolerance=±5% resistance=330 package=THT]
  LED2 = LED - 5mm [color="Green (560nm)" package="5 mm [THT]"]
  R2 = Resistor [tolerance=±5% resistance=330 package=THT]
  LED3 = LED - 5mm [color="Red (633nm)" package="5 mm [THT]"]

nets:
  3V3: Raspberry_Pi_1.3v3, Raspberry_Pi_1.3V3, Play_Pause.Pin_3, Play_Pause.Pin_4, Back.Pin_3, Back.Pin_4
  N1: Raspberry_Pi_1.GND, R1.Pin_1, R2.Pin_1
  N2: Raspberry_Pi_1.GPIO17, LED3.anode
  N3: Raspberry_Pi_1.GPIO25, Play_Pause.Pin_1, Play_Pause.Pin_2
  N4: Raspberry_Pi_1.GPIO24, Back.Pin_1, Back.Pin_2
  N5: Raspberry_Pi_1.GPIO18, LED2.anode
  N6: R1.Pin_0, LED2.cathode
  N7: R2.Pin_0, LED3.cathode

notes:
  Play Pause (25)
  Back (24)
  Play (18)
  Power (17)
